# Fritzing sketch wiring-diagram (saved by Fritzing 0.9.2b)
breadboards: 3

parts:
  Parte1 = Motor Driver 1A Dual TB6612FNG  # not connected
  Parte2 = Motor Driver 1A Dual TB6612FNG  # not connected
  U1 = LM2596 step down module
  Parte3 = Arduino Mega 2560 (Rev3)
  M1 = damikro tbs mini
  Parte4 = Motor Driver 1A Dual TB6612FNG  # not connected
  SP1 = SPEAKER [package=pcb_mount_speaker]

nets:
  N1: U1.IN-, U1.OUT-, Parte3.GND, M1.SP-GND, M1.Prop1_input_gnd, M1.Out_3+4_gnd, M1.Prog_GND
  N2: U1.OUT+, M1.Prop1_input_pwr, M1.Out_1+2_pwr
  N3: Parte3.D49, M1.Prop1_input_sig, M1.Prop1_output_sig
  N4: Parte3.D51, M1.Prop2_input_sig
  N5: Parte3.D53, M1.Prop3_input_sig
  N6: M1.SP+, SP1.-
  N7: M1.SP-, SP1.+

notes:
  14,6V Battery (to 7,2V)
  [smoke generator, smoke fan], [left motor, right motor], [gun elevation, turret rotation]
  PS2 Controller
  -------------------
  1 Acknoledge
  2 N/A
  3 Clock
  4 Attention
  5 Power 3.3V
  6 Ground
  7 N/A
  8 Command
  9 Data

custom parts:
  LM2596 step down module: LM2596 DC-DC step down power supply module 3 A.
  damikro tbs mini: damikro tbs mini digital multifunctional RC sound unit. Pcb view has been omitted as not useful.
